# Fritzing sketch 2led (saved by Fritzing 0.9.4)
breadboards: 1

parts:
  LED1 = smd LED [color="Red (633nm)" package="1206 [SMD]"]
  LED2 = smd LED [color="Red (633nm)" package="1206 [SMD]"]
  Part1 = Arduino Uno (Rev3) - ICSP
  R1 = Resistor [tolerance=±5% resistance=220 package=THT]
  R2 = Resistor [tolerance=±5% resistance=220 package=THT]

nets:
  N1: LED1.cathode, R1.Pin_1
  N2: LED1.anode, Part1.D9_PWM
  N3: LED2.cathode, R2.Pin_1
  N4: LED2.anode, Part1.D13/SCK
  N5: Part1.GND, R1.Pin_0, R2.Pin_0
